// Logisim project (CSB19057)   8X3 priority encoder 2.circ as structural Verilog: 1 circuit, main circuit main
module main (
  input  _0,
  input  _1,
  input  _2,
  input  _3,
  input  _4,
  input  _5,
  input  _6,
  input  _7,
  output Y2,
  output Y1,
  output Y0,
  output V
);

  or or_1 (Y2, _7, _6, _5, _4);
  or or_2 (Y1, _7, _6, _4, _3);
  or or_3 (Y0, _7, _5, _3, _1);
  or or_4 (V, _7, _6, _5, _4, _3, _2, _1, _0);
endmodule
