// Logisim project 16x1 mux.circ as structural Verilog: 2 circuits, main circuit main
module main (
  input  I15,
  input  I14,
  input  I13,
  input  I12,
  input  I11,
  input  I10,
  input  I9,
  input  I8,
  input  I7,
  input  I6,
  input  I5,
  input  I4,
  input  A2,
  input  A3,
  input  I3,
  input  I2,
  input  I1,
  input  I0,
  input  A0,
  input  A1,
  output out_21
);

  wire n4x1_mux_1_out_7, n4x1_mux_2_out_7, n4x1_mux_3_out_7, n4x1_mux_4_out_7;

  _4x1_mux u_4x1_mux_1 (.out_7(n4x1_mux_1_out_7), .I3(I15), .I2(I14), .I1(I13), .I0(I12), .S1(A1), .S0(A0));
  _4x1_mux u_4x1_mux_2 (.out_7(n4x1_mux_2_out_7), .I3(I11), .I2(I10), .I1(I9), .I0(I8), .S1(A1), .S0(A0));
  _4x1_mux u_4x1_mux_3 (.out_7(n4x1_mux_3_out_7), .I3(I7), .I2(I6), .I1(I5), .I0(I4), .S1(A1), .S0(A0));
  _4x1_mux u_4x1_mux_4 (.out_7(n4x1_mux_4_out_7), .I3(I3), .I2(I2), .I1(I1), .I0(I0), .S1(A1), .S0(A0));
  _4x1_mux u_4x1_mux_5 (
    .out_7(out_21), .I3(n4x1_mux_1_out_7), .I2(n4x1_mux_2_out_7), .I1(n4x1_mux_3_out_7),
    .I0(n4x1_mux_4_out_7), .S1(A3), .S0(A2));

  // Notes on the sheet:
  //   CSB19057
  //   PRASANJIT DUTTA
endmodule

module _4x1_mux (
  input  I3,
  input  I2,
  input  I1,
  input  I0,
  input  S1,
  input  S0,
  output out_7
);

  wire and_1_out, and_2_out, and_3_out, and_4_out, not_1_out, not_2_out;

  not not_1 (not_1_out, S0);
  not not_2 (not_2_out, S1);
  and and_1 (and_1_out, S1, S0, I3);
  and and_2 (and_2_out, S1, not_1_out, I2);
  and and_3 (and_3_out, not_2_out, S0, I1);
  and and_4 (and_4_out, not_2_out, not_1_out, I0);
  or or_1 (out_7, and_1_out, and_2_out, and_3_out, and_4_out);
endmodule
