// Logisim project 4bit adder.circ as structural Verilog: 1 circuit, main circuit main
module main (
  input  A0,
  input  B0,
  input  A1,
  input  B1,
  input  A2,
  input  B2,
  input  B3,
  input  in_8,
  input  in_9,
  output Cout,
  output S3,
  output S0,
  output S1,
  output S2
);

  wire adder_2_cout, adder_3_cout, adder_4_cout;

  Adder #(.width(1)) adder_1 (.a(B0), .b(A0), .out(S0), .cin(adder_2_cout), .cout(Cout));
  Adder #(.width(1)) adder_2 (.a(B1), .b(A1), .out(S1), .cin(adder_3_cout), .cout(adder_2_cout));
  Adder #(.width(1)) adder_3 (.a(B2), .b(A2), .out(S2), .cin(adder_4_cout), .cout(adder_3_cout));
  Adder #(.width(1)) adder_4 (.a(in_8), .b(B3), .out(S3), .cin(in_9), .cout(adder_4_cout));

  // Notes on the sheet:
  //   C2
  //   C1
  //   A3
  //   C0
  //   Cin
endmodule
