// Logisim project 4bit cla adder.circ as structural Verilog: 2 circuits, main circuit main
module main (
  input  A3,
  input  B3,
  input  A2,
  input  B2,
  input  A1,
  input  B1,
  input  A0,
  input  B0,
  input  C0,
  output S3,
  output S2,
  output S1,
  output S0,
  output C4
);

  wire combination_ckt_1_out_10, combination_ckt_1_out_11, combination_ckt_1_out_12;

  Adder #(.width(1)) adder_1 (.a(A3), .b(B3), .out(S3), .cin(combination_ckt_1_out_12));  // open: cout
  Adder #(.width(1)) adder_2 (.a(A2), .b(B2), .out(S2), .cin(combination_ckt_1_out_11));  // open: cout
  Adder #(.width(1)) adder_3 (.a(A1), .b(B1), .out(S1), .cin(combination_ckt_1_out_10));  // open: cout
  Adder #(.width(1)) adder_4 (.a(B0), .b(A0), .out(S0), .cin(C0));  // open: cout
  combination_ckt combination_ckt_1 (
    .in_1(A0), .in_2(B0), .in_3(C0), .in_4(A1), .in_5(B1), .in_6(A2), .in_7(B2), .in_8(A3), .in_9(B3),
    .out_10(combination_ckt_1_out_10), .out_11(combination_ckt_1_out_11), .out_12(combination_ckt_1_out_12),
    .out_13(C4));

  // Notes on the sheet:
  //   /Cout
  //   CSB19057
  //   PRASANJIT DUTTA
endmodule

module combination_ckt (
  input  in_1,
  input  in_2,
  input  in_3,
  input  in_4,
  input  in_5,
  input  in_6,
  input  in_7,
  input  in_8,
  input  in_9,
  output out_10,
  output out_11,
  output out_12,
  output out_13
);

  wire and_1_out, and_2_out, and_3_out, and_4_out, and_5_out, and_6_out, and_7_out, and_8_out, xor_1_out,
       xor_2_out, xor_3_out, xor_4_out;

  xor xor_1 (xor_1_out, in_8, in_9);
  xor xor_2 (xor_2_out, in_1, in_2);
  and and_1 (and_1_out, in_2, in_1);
  xor xor_3 (xor_3_out, in_4, in_5);
  and and_2 (and_2_out, in_5, in_4);
  xor xor_4 (xor_4_out, in_6, in_7);
  and and_3 (and_3_out, in_7, in_6);
  and and_4 (and_4_out, in_9, in_8);
  and and_5 (and_5_out, out_12, xor_1_out);
  and and_6 (and_6_out, in_3, xor_2_out);
  and and_7 (and_7_out, out_10, xor_3_out);
  and and_8 (and_8_out, out_11, xor_4_out);
  or or_1 (out_10, and_6_out, and_1_out);
  or or_2 (out_11, and_7_out, and_2_out);
  or or_3 (out_12, and_8_out, and_3_out);
  or or_4 (out_13, and_5_out, and_4_out);
endmodule
