// Logisim project 4x1 mux full adder.circ as structural Verilog: 1 circuit, main circuit main
module main (
  input  A,
  input  _0,
  input  [1:0] B,
  output out_4,
  output Sum
);

  wire not_1_out, not_2_out;

  not not_1 (not_1_out, A);
  not not_2 (not_2_out, _0);
  Multiplexer #(.select(2)) multiplexer_1 (
    .in0(A), .in1(not_1_out), .in2(not_1_out), .in3(A), .out(Sum), .sel(B));  // open: en
  Multiplexer #(.select(2)) multiplexer_2 (
    .in0(_0), .in1(A), .in2(A), .in3(not_2_out), .out(out_4), .sel(B));  // open: en

  // Notes on the sheet:
  //   C
  //   carry
endmodule
