// Logisim project 4x1 mux full subtractor.circ as structural Verilog: 1 circuit, main circuit main
module main (
  input  A,
  input  _0,
  input  _0_2,
  input  [1:0] B,
  output out_5,
  output difference
);

  wire not_1_out, not_2_out, not_3_out, not_4_out;

  not not_1 (not_1_out, _0_2);
  not not_2 (not_2_out, A);
  not not_3 (not_3_out, _0);
  Multiplexer #(.select(2)) multiplexer_1 (
    .in0(not_1_out), .in1(_0_2), .in2(not_2_out), .in3(A), .out(difference), .sel(B));  // open: en
  not not_4 (not_4_out, A);
  Multiplexer #(.select(2)) multiplexer_2 (
    .in0(_0), .in1(not_4_out), .in2(not_4_out), .in3(not_3_out), .out(out_5), .sel(B));  // open: en

  // Notes on the sheet:
  //   C
  //   borrow
endmodule
