// Logisim project 8x1 mux full subtractor.circ as structural Verilog: 1 circuit, main circuit main
module main (
  input  _0,
  input  [2:0] in_2,
  output out_3,
  output out_4
);

  wire not_1_out;

  not not_1 (not_1_out, _0);
  Multiplexer #(.select(3)) multiplexer_1 (
    .in0(_0), .in1(not_1_out), .in2(not_1_out), .in3(_0), .in4(not_1_out), .in5(_0), .in6(_0),
    .in7(not_1_out), .out(out_3), .sel(in_2));  // open: en
  Multiplexer #(.select(3)) multiplexer_2 (
    .in0(_0), .in1(not_1_out), .in2(not_1_out), .in3(not_1_out), .in4(_0), .in5(_0), .in6(_0),
    .in7(not_1_out), .out(out_4), .sel(in_2));  // open: en
endmodule
