// Logisim project Binary to gray code converter.circ as structural Verilog: 1 circuit, main circuit main
module main (
  input  A,
  input  B,
  input  C,
  input  D,
  output G4,
  output G3,
  output G2,
  output G1
);

  xor xor_1 (G3, A, B);
  xor xor_2 (G2, B, C);
  xor xor_3 (G1, C, D);

  assign G4 = A;

  // Notes on the sheet:
  //   PRASANJT DUTTA
  //   CSB19057
endmodule
