// Logisim project D flip flop.circ as structural Verilog: 1 circuit, main circuit main
module main (
  input  D,
  output Q,
  output Q_prime
);

  wire clock_1_out, nand_1_out, nand_2_out, not_1_out;

  not not_1 (not_1_out, D);
  Clock clock_1 (.out(clock_1_out));
  nand nand_1 (nand_1_out, D, clock_1_out);
  nand nand_2 (nand_2_out, clock_1_out, not_1_out);
  nand nand_3 (Q, nand_1_out, Q_prime);
  nand nand_4 (Q_prime, Q, nand_2_out);

  // Notes on the sheet:
  //   clk
endmodule
