// Logisim project Gray to binary converter.circ as structural Verilog: 1 circuit, main circuit main
module main (
  input  G4,
  input  G3,
  input  G2,
  input  G1,
  output B4,
  output B3,
  output B2,
  output B1
);

  xor xor_1 (B4, G4, B3);
  buf xor_2 (B3, G3);  // XOR_Gate
  xor xor_3 (G3, G2, G1);

  assign B1 = G1;
  assign B2 = G3;

  // Notes on the sheet:
  //   CSB19057
  //   PRASANJIT DUTTA
endmodule
