// Logisim project JK to D Flip Flop.circ as structural Verilog: 1 circuit, main circuit main
module main (
  input  D,
  output Q,
  output Q_prime
);

  wire clock_1_out, not_1_out;

  Clock clock_1 (.out(clock_1_out));
  not not_1 (not_1_out, D);
  J_K_Flip_Flop j_k_ff_1 (.J(D), .clk(clock_1_out), .K(not_1_out), .Q(Q), .Qn(Q_prime));  // open: preset, en, reset

  // Notes on the sheet:
  //   Clk
  //   JK to D Flip-Flop
  //   JK Flip-Flop
endmodule
