// Logisim project full adder using 3x8 decocer.circ as structural Verilog: 2 circuits, main circuit main
module main (
  input  A,
  input  B,
  input  C,
  output Sum,
  output Cout
);

  wire n3x8_decoder_1__0, n3x8_decoder_1_out_5, n3x8_decoder_1_out_6, n3x8_decoder_1_out_7,
       n3x8_decoder_1_out_8, n3x8_decoder_1_out_9, n3x8_decoder_1_out_10, n3x8_decoder_1_out_11;

  _3x8_decoder u_3x8_decoder_1 (
    ._0(n3x8_decoder_1__0), .out_5(n3x8_decoder_1_out_5), .out_6(n3x8_decoder_1_out_6),
    .out_7(n3x8_decoder_1_out_7), .out_8(n3x8_decoder_1_out_8), .out_9(n3x8_decoder_1_out_9),
    .out_10(n3x8_decoder_1_out_10), .out_11(n3x8_decoder_1_out_11), .in_1(A), .in_2(B), .in_3(C));
  or or_1 (Sum, n3x8_decoder_1_out_5, n3x8_decoder_1_out_6, n3x8_decoder_1_out_8, n3x8_decoder_1_out_11);
  or or_2 (Cout, n3x8_decoder_1_out_11, n3x8_decoder_1_out_7, n3x8_decoder_1_out_9, n3x8_decoder_1_out_10);

  // Notes on the sheet:
  //    0
  //    1
  //    2
  //    3
  //    4
  //    5
  //    6
  //    7
endmodule

module _3x8_decoder (
  input  in_1,
  input  in_2,
  input  in_3,
  output _0,
  output out_5,
  output out_6,
  output out_7,
  output out_8,
  output out_9,
  output out_10,
  output out_11
);

  wire not_1_out, not_2_out, not_3_out;

  not not_1 (not_1_out, in_1);
  not not_2 (not_2_out, in_2);
  not not_3 (not_3_out, in_3);
  and and_1 (_0, not_1_out, not_2_out, not_3_out);
  and and_2 (out_5, not_1_out, not_2_out, in_3);
  and and_3 (out_6, not_1_out, in_2, not_3_out);
  and and_4 (out_7, not_1_out, in_2, in_3);
  and and_5 (out_8, in_1, not_2_out, not_3_out);
  and and_6 (out_9, in_1, not_2_out, in_3);
  and and_7 (out_10, in_1, in_2, not_3_out);
  and and_8 (out_11, in_1, in_2, in_3);
endmodule
