// Logisim project full subtractor.circ as structural Verilog: 1 circuit, main circuit main
module main (
  input  a,
  input  b,
  input  Cin,
  output Diff,
  output Borr
);

  wire and_1_out, and_2_out, not_1_out, not_2_out, xor_1_out;

  xor xor_1 (xor_1_out, a, b);
  not not_1 (not_1_out, Cin);
  not not_2 (not_2_out, b);
  xor xor_2 (Diff, xor_1_out, Cin);
  and and_1 (and_1_out, not_1_out, xor_1_out);
  and and_2 (and_2_out, not_2_out, a);
  or or_1 (Borr, and_1_out, and_2_out);
endmodule
