// Logisim project half adder.circ as structural Verilog: 1 circuit, main circuit main
module main (
  input  A,
  input  B,
  output x,
  output y
);

  xor xor_1 (x, A, B);
  and and_1 (y, A, B);
endmodule
