// Logisim project half subtractor.circ as structural Verilog: 1 circuit, main circuit main
module main (
  input  A,
  input  B,
  output x,
  output y
);

  wire not_1_out;

  not not_1 (not_1_out, A);
  xor xor_1 (x, A, B);
  and and_1 (y, not_1_out, B);
endmodule
